# Fritzing sketch PompeVideRegulationLight_V0 (saved by Fritzing 0.9.3b)
circuit board: 10cm x 6.7cm
breadboards: 1

parts:
  HLK-PM1 = HLK-PM01
  MPX1 = MPX5100 pressure sensor [part_number=MPX]
  Composant1 = Arduino Uno (Rev3)
  J1 = screw terminal, 2 pins
  J2 = screw terminal, 2 pins
  J3 = screw terminal, 2 pins
  J4 = screw terminal, 2 pins
  J5 = screw terminal, 2 pins
  J6 = screw terminal, 2 pins
  J7 = screw terminal, 2 pins

nets:
  N1: HLK-PM1.AC#0, J1.pin1
  N2: HLK-PM1.AC#1, J1.pin2
  GND: HLK-PM1.-Vo, MPX1.GND, Composant1.GND, J3.pin1, J6.pin1, J7.pin1
  N3: HLK-PM1.+Vo, Composant1.VIN
  N4: MPX1.V_out, Composant1.A0
  N5: MPX1.Vs, Composant1.5V, J3.pin2, J7.pin2
  N6: Composant1.D11_PWM/MOSI, J6.pin2
  N7: Composant1.A4/SDA, J2.pin2
  N8: Composant1.A5/SCL, J2.pin1
  N9: Composant1.D2, J4.pin2
  N10: Composant1.D3_PWM, J4.pin1
  N11: Composant1.D4, J5.pin2
  N12: Composant1.D5_PWM, J5.pin1

notes:
  220V
  5V
  MPX5100DP
  Vacuum controller Light V0
  |    LCD   |
  Relay
  |   Rotary   |
  SCL
  SDA
  -
  +
  SW
  DT
  CLK
  zinktiti@hotmail.fr
  /!\

custom parts:
  MPX5100 pressure sensor: MPX5100 Integrated Silicon Pressure Sensor On-Chip Signal Conditioned, Temperature Compensated and Calibrated The MPX5100 series piezoresistive transducer is a state-of-the-art monolithic silicon pressure sensor designed for a wide range of applications, but particularly those employing a microcontroller or microprocessor with A/D inputs. This patented, single element transducer combines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
