# Fritzing sketch PompeVideRegulationLight_V1 (saved by Fritzing 1.0.4)
circuit board: 10.7074cm x 6.7cm

parts:
  HLK-PM1 = HLK-PM01
  Arduino_UNO = Arduino Uno (Rev3)
  F1 = FUSE [package=fuse_5mm]
  F2 = FUSE [package=fuse_5mm]
  MPX5100DP = MPX5100 pressure sensor [part_number=MPX]
  DT/CLK = screw terminal, 2 pins
  SCL/SDA = screw terminal, 2 pins
  -/+ = screw terminal, 2 pins
  +/- = screw terminal, 2 pins
  +/-_2 = screw terminal, 2 pins
  SW/ = screw terminal, 2 pins
  POWER_IN = screw terminal, 2 pins

nets:
  N1: HLK-PM1.AC#0, F1.2
  N2: HLK-PM1.AC#1, POWER_IN.pin2
  GND: HLK-PM1.-Vo, Arduino_UNO.GND, MPX5100DP.GND, -/+.pin1, +/-.pin1, +/-_2.pin1
  N3: HLK-PM1.+Vo, F2.1
  N4: Arduino_UNO.A0, MPX5100DP.V_out
  N5: Arduino_UNO.D11_PWM/MOSI, +/-.pin2
  N6: Arduino_UNO.A4/SDA, SCL/SDA.pin2
  N7: Arduino_UNO.A5/SCL, SCL/SDA.pin1
  N8: Arduino_UNO.D2, DT/CLK.pin2
  N9: Arduino_UNO.D3_PWM, DT/CLK.pin1
  N10: Arduino_UNO.D4, SW/.pin2
  N11: Arduino_UNO.D5_PWM, SW/.pin1
  N12: Arduino_UNO.5V, MPX5100DP.Vs, -/+.pin2, +/-_2.pin2
  N13: Arduino_UNO.VIN, F2.2
  N14: F1.1, POWER_IN.pin1

notes:
  220V
  5V
  MPX5100DP
  Vacuum controller Light V1
  |    LCD   |
  Relay
  |     Rotary    |
  SCL
  SDA
  -
  +
  SW
  DT
  CLK
  zinktiti@hotmail.fr
  /!\
  LCD
  Rotate

custom parts:
  MPX5100 pressure sensor: MPX5100 Integrated Silicon Pressure Sensor On-Chip Signal Conditioned, Temperature Compensated and Calibrated The MPX5100 series piezoresistive transducer is a state-of-the-art monolithic silicon pressure sensor designed for a wide range of applications, but particularly those employing a microcontroller or microprocessor with A/D inputs. This patented, single element transducer combines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
