# Fritzing sketch PompeVideRegulationLight_V1 (saved by Fritzing 1.0.2b)
circuit board: 10.7074cm x 6.7cm
breadboards: 1

parts:
  HLK-PM1 = HLK-PM01
  MPX5100DP = MPX5100 pressure sensor [part_number=MPX]
  Composant1 = Arduino Uno (Rev3)
  POWER_IN = screw terminal, 2 pins
  SCL/SDA = screw terminal, 2 pins
  -/+ = screw terminal, 2 pins
  DT/CLK = screw terminal, 2 pins
  SW/ = screw terminal, 2 pins
  +/- = screw terminal, 2 pins
  +/-_2 = screw terminal, 2 pins
  F1 = FUSE [package=fuse_5mm]
  F2 = FUSE [package=fuse_5mm]

nets:
  N1: HLK-PM1.AC#0, F1.2
  N2: HLK-PM1.AC#1, POWER_IN.pin2
  GND: HLK-PM1.-Vo, MPX5100DP.GND, Composant1.GND, -/+.pin1, +/-.pin1, +/-_2.pin1
  N3: HLK-PM1.+Vo, F2.1
  N4: MPX5100DP.V_out, Composant1.A0
  N5: MPX5100DP.Vs, Composant1.5V, -/+.pin2, +/-_2.pin2
  N6: Composant1.D11_PWM/MOSI, +/-.pin2
  N7: Composant1.A4/SDA, SCL/SDA.pin2
  N8: Composant1.A5/SCL, SCL/SDA.pin1
  N9: Composant1.D2, DT/CLK.pin2
  N10: Composant1.D3_PWM, DT/CLK.pin1
  N11: Composant1.D4, SW/.pin2
  N12: Composant1.D5_PWM, SW/.pin1
  N13: Composant1.VIN, F2.2
  N14: POWER_IN.pin1, F1.1

notes:
  220V
  5V
  MPX5100DP
  Vacuum controller Light V1
  |    LCD   |
  Relay
  |     Rotary    |
  SCL
  SDA
  -
  +
  SW
  DT
  CLK
  zinktiti@hotmail.fr
  /!\
  LCD
  Rotate

custom parts:
  MPX5100 pressure sensor: MPX5100 Integrated Silicon Pressure Sensor On-Chip Signal Conditioned, Temperature Compensated and Calibrated The MPX5100 series piezoresistive transducer is a state-of-the-art monolithic silicon pressure sensor designed for a wide range of applications, but particularly those employing a microcontroller or microprocessor with A/D inputs. This patented, single element transducer combines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
